// Logisim project lesson1.circ as structural Verilog
module customNOT (
  input  A,
  output Y
);

  nand nand_1 (Y, A, A);
endmodule

module customAND (
  input  A,
  input  B,
  output Y
);

  wire nand_1_out;

  nand nand_1 (nand_1_out, A, B);
  customNOT customnot_1 (.A(nand_1_out), .Y(Y));
endmodule

module customOR (
  input  A,
  input  B,
  output Y
);

  wire customand_1_y, customnot_1_y, customnot_2_y;

  customNOT customnot_1 (.A(A), .Y(customnot_1_y));
  customNOT customnot_2 (.A(B), .Y(customnot_2_y));
  customAND customand_1 (.A(customnot_1_y), .B(customnot_2_y), .Y(customand_1_y));
  customNOT customnot_3 (.A(customand_1_y), .Y(Y));
endmodule

module customXOR (
  input  A,
  input  B,
  output Y
);

  wire customand_1_y, customand_2_y, customnot_1_y, customnot_2_y;

  customNOT customnot_1 (.A(B), .Y(customnot_1_y));
  customNOT customnot_2 (.A(A), .Y(customnot_2_y));
  customAND customand_1 (.A(A), .B(customnot_1_y), .Y(customand_1_y));
  customAND customand_2 (.A(customnot_2_y), .B(B), .Y(customand_2_y));
  customOR customor_1 (.A(customand_1_y), .B(customand_2_y), .Y(Y));
endmodule

module customMUX (
  input  A,
  input  sel,
  input  B,
  output Y
);

  wire customand_1_y, customand_2_y, customnot_1_y;

  customNOT customnot_1 (.A(sel), .Y(customnot_1_y));
  customAND customand_1 (.A(A), .B(customnot_1_y), .Y(customand_1_y));
  customAND customand_2 (.A(sel), .B(B), .Y(customand_2_y));
  customOR customor_1 (.A(customand_1_y), .B(customand_2_y), .Y(Y));
endmodule

module customDMUX (
  input  inp,
  input  sel,
  output A,
  output B
);

  wire customnot_1_y;

  customNOT customnot_1 (.A(sel), .Y(customnot_1_y));
  customAND customand_1 (.A(inp), .B(customnot_1_y), .Y(A));
  customAND customand_2 (.A(sel), .B(inp), .Y(B));
endmodule

module customNOT4 (
  input  [3:0] A,
  output [3:0] Y
);

  customNOT customnot_1 (.A(A[0]), .Y(Y[0]));
  customNOT customnot_2 (.A(A[1]), .Y(Y[1]));
  customNOT customnot_3 (.A(A[2]), .Y(Y[2]));
  customNOT customnot_4 (.A(A[3]), .Y(Y[3]));
endmodule

module customAND4 (
  input  [3:0] A,
  input  [3:0] B,
  output [3:0] Y
);

  customAND customand_1 (.A(A[0]), .B(B[0]), .Y(Y[0]));
  customAND customand_2 (.A(A[1]), .B(B[1]), .Y(Y[1]));
  customAND customand_3 (.A(A[2]), .B(B[2]), .Y(Y[2]));
  customAND customand_4 (.A(A[3]), .B(B[3]), .Y(Y[3]));
endmodule

module customOR4 (
  input  [3:0] A,
  input  [3:0] B,
  output [3:0] Y
);

  customOR customor_1 (.A(A[0]), .B(B[0]), .Y(Y[0]));
  customOR customor_2 (.A(A[1]), .B(B[1]), .Y(Y[1]));
  customOR customor_3 (.A(A[2]), .B(B[2]), .Y(Y[2]));
  customOR customor_4 (.A(A[3]), .B(B[3]), .Y(Y[3]));
endmodule

module customMUX4 (
  input  [3:0] A,
  input  sel,
  input  [3:0] B,
  output [3:0] Y
);

  customMUX custommux_1 (.A(A[0]), .sel(sel), .B(B[0]), .Y(Y[0]));
  customMUX custommux_2 (.A(A[1]), .sel(sel), .B(B[1]), .Y(Y[1]));
  customMUX custommux_3 (.A(A[2]), .sel(sel), .B(B[2]), .Y(Y[2]));
  customMUX custommux_4 (.A(A[3]), .sel(sel), .B(B[3]), .Y(Y[3]));
endmodule

module customOR8WAY (
  input  [7:0] A,
  output Y
);

  wire customor_1_y, customor_2_y, customor_3_y, customor_4_y, customor_5_y, customor_6_y;

  customOR customor_1 (.A(A[0]), .B(A[1]), .Y(customor_1_y));
  customOR customor_2 (.A(customor_1_y), .B(A[2]), .Y(customor_2_y));
  customOR customor_3 (.A(customor_2_y), .B(A[3]), .Y(customor_3_y));
  customOR customor_4 (.A(customor_3_y), .B(A[4]), .Y(customor_4_y));
  customOR customor_5 (.A(customor_4_y), .B(A[5]), .Y(customor_5_y));
  customOR customor_6 (.A(customor_5_y), .B(A[6]), .Y(customor_6_y));
  customOR customor_7 (.A(customor_6_y), .B(A[7]), .Y(Y));
endmodule

module customMUX4WAY4 (
  input  [3:0] A,
  input  [3:0] B,
  input  [1:0] sel,
  input  [3:0] C,
  input  [3:0] D,
  output [3:0] Y
);

  wire [3:0] custommux4_1_y, custommux4_2_y;

  customMUX4 custommux4_1 (.A(A), .sel(sel[0]), .B(B), .Y(custommux4_1_y));
  customMUX4 custommux4_2 (.A(C), .sel(sel[0]), .B(D), .Y(custommux4_2_y));
  customMUX4 custommux4_3 (.A(custommux4_1_y), .sel(sel[1]), .B(custommux4_2_y), .Y(Y));
endmodule

module customMUX8WAY4 (
  input  [3:0] A,
  input  [3:0] B,
  input  [3:0] C,
  input  [2:0] sel,
  input  [3:0] D,
  input  [3:0] E,
  input  [3:0] F,
  input  [3:0] G,
  input  [3:0] H,
  output [3:0] Y
);

  wire [3:0] custommux4_1_y, custommux4_2_y, custommux4_3_y, custommux4_4_y, custommux4_5_y, custommux4_6_y;

  customMUX4 custommux4_1 (.A(A), .sel(sel[0]), .B(B), .Y(custommux4_1_y));
  customMUX4 custommux4_2 (.A(C), .sel(sel[0]), .B(D), .Y(custommux4_2_y));
  customMUX4 custommux4_3 (.A(E), .sel(sel[0]), .B(F), .Y(custommux4_3_y));
  customMUX4 custommux4_4 (.A(G), .sel(sel[0]), .B(H), .Y(custommux4_4_y));
  customMUX4 custommux4_5 (.A(custommux4_1_y), .sel(sel[1]), .B(custommux4_2_y), .Y(custommux4_5_y));
  customMUX4 custommux4_6 (.A(custommux4_3_y), .sel(sel[1]), .B(custommux4_4_y), .Y(custommux4_6_y));
  customMUX4 custommux4_7 (.A(custommux4_5_y), .sel(sel[2]), .B(custommux4_6_y), .Y(Y));
endmodule

module customDMUX4 (
  input  inSig,
  input  [1:0] sel,
  output A,
  output B,
  output C,
  output D
);

  wire customdmux_1_a, customdmux_1_b;

  customDMUX customdmux_1 (.inp(inSig), .sel(sel[1]), .A(customdmux_1_a), .B(customdmux_1_b));
  customDMUX customdmux_2 (.inp(customdmux_1_a), .sel(sel[0]), .A(A), .B(B));
  customDMUX customdmux_3 (.inp(customdmux_1_b), .sel(sel[0]), .A(C), .B(D));
endmodule

module customDMUX8 (
  input  inpSig,
  input  [2:0] sel,
  output A,
  output B,
  output C,
  output D,
  output E,
  output F,
  output G,
  output H
);

  wire customdmux4_1_a, customdmux4_1_b, customdmux4_1_c, customdmux4_1_d;

  customDMUX4 customdmux4_1 (
    .inSig(inpSig), .sel(sel[2:1]), .A(customdmux4_1_a), .B(customdmux4_1_b), .C(customdmux4_1_c),
    .D(customdmux4_1_d));
  customDMUX customdmux_1 (.inp(customdmux4_1_a), .sel(sel[0]), .A(A), .B(B));
  customDMUX customdmux_2 (.inp(customdmux4_1_b), .sel(sel[0]), .A(C), .B(D));
  customDMUX customdmux_3 (.inp(customdmux4_1_c), .sel(sel[0]), .A(E), .B(F));
  customDMUX customdmux_4 (.inp(customdmux4_1_d), .sel(sel[0]), .A(G), .B(H));
endmodule
