// Logisim project lesson2.circ as structural Verilog
module halfAdder (
  input  A,
  input  B,
  output sum,
  output carry
);

  and and_1 (carry, A, B);
  xor xor_1 (sum, A, B);
endmodule

module fullAdder (
  input  A,
  input  B,
  input  C,
  output sum,
  output carry
);

  wire halfadder_1_carry, halfadder_1_sum, halfadder_2_carry;

  halfAdder halfadder_1 (.A(A), .B(B), .sum(halfadder_1_sum), .carry(halfadder_1_carry));
  halfAdder halfadder_2 (.A(C), .B(halfadder_1_sum), .sum(sum), .carry(halfadder_2_carry));
  or or_1 (carry, halfadder_1_carry, halfadder_2_carry);
endmodule

module fourBitAdder (
  input  [3:0] A,
  input  Cin,
  input  [3:0] B,
  output [3:0] sum,
  output carry
);

  wire fulladder_1_carry, fulladder_2_carry, fulladder_3_carry;

  fullAdder fulladder_1 (.A(A[0]), .B(B[0]), .C(Cin), .sum(sum[0]), .carry(fulladder_1_carry));
  fullAdder fulladder_2 (.A(A[1]), .B(B[1]), .C(fulladder_1_carry), .sum(sum[1]), .carry(fulladder_2_carry));
  fullAdder fulladder_3 (.A(A[2]), .B(B[2]), .C(fulladder_2_carry), .sum(sum[2]), .carry(fulladder_3_carry));
  fullAdder fulladder_4 (.A(A[3]), .B(B[3]), .C(fulladder_3_carry), .sum(sum[3]), .carry(carry));
endmodule

module fourBitIncrementer (
  input  [3:0] A,
  output [3:0] Y
);

  fourBitAdder fourbitadder_1 (.A(A), .B(4'b0001), .sum(Y));  // open: Cin, carry
endmodule

module fourBitSubstractor (
  input  [3:0] A,
  input  [3:0] B,
  output [3:0] Y,
  output carry
);

  wire [3:0] not_1_out;

  assign not_1_out = ~B;  // NOT_Gate not_1, 4 bits wide
  fourBitAdder fourbitadder_1 (.A(A), .Cin(1'b1), .B(not_1_out), .sum(Y), .carry(carry));
endmodule

module fourBitAdderSubstractor (
  input  [3:0] A,
  input  [3:0] B,
  input  K,
  output [3:0] Y,
  output carry
);

  wire [3:0] multiplexer_1_out, not_1_out;

  assign not_1_out = ~B;  // NOT_Gate not_1, 4 bits wide
  Multiplexer #(.width(4), .enable("false")) multiplexer_1 (.in0(B), .in1(not_1_out), .out(multiplexer_1_out), .sel(K));
  fourBitAdder fourbitadder_1 (.A(A), .Cin(K), .B(multiplexer_1_out), .sum(Y), .carry(carry));
endmodule

module overflow (
  input  [3:0] A,
  input  [3:0] B,
  input  addOrSub,
  output V,
  output [3:0] Y
);

  wire bitselector_1_out, bitselector_2_out;

  BitSelector #(.width(4)) bitselector_1 (.in(A), .out(bitselector_1_out), .sel(2'b11));
  xor xor_1 (V, bitselector_1_out, bitselector_2_out);
  BitSelector #(.width(4)) bitselector_2 (.in(Y), .out(bitselector_2_out), .sel(2'b11));
  fourBitAdderSubstractor fourbitaddersubstractor_1 (.A(A), .B(B), .K(addOrSub), .Y(Y));  // open: carry
endmodule

module equalityComp (
  input  [3:0] A,
  input  [3:0] B,
  output Y
);

  wire xnor_1_out, xnor_2_out, xnor_3_out, xnor_4_out;

  xnor xnor_1 (xnor_1_out, A[0], B[0]);
  xnor xnor_2 (xnor_2_out, A[1], B[1]);
  xnor xnor_3 (xnor_3_out, A[2], B[2]);
  xnor xnor_4 (xnor_4_out, A[3], B[3]);
  and and_1 (Y, xnor_1_out, xnor_2_out, xnor_3_out, xnor_4_out);
endmodule

module magnitudeComp (
  input  [3:0] A,
  input  [3:0] B,
  output ALessThanB
);

  wire [3:0] fourbitsubstractor_1_y;

  fourBitSubstractor fourbitsubstractor_1 (.A(A), .B(B), .Y(fourbitsubstractor_1_y));  // open: carry
  BitSelector #(.width(4)) bitselector_1 (.in(fourbitsubstractor_1_y), .out(ALessThanB), .sel(2'b11));
endmodule

module ALU (
  input  [2:0] ALUControl,
  input  [31:0] B,
  input  [31:0] A,
  output [31:0] Result,
  output Negative,
  output Zero
);

  wire bitselector_1_out, or32_1_y;
  wire [31:0] adder_1_out, and_1_out, multiplexer_1_out, not_1_out, or_1_out, zeroextend_1_y;

  Multiplexer #(.width(32), .enable("false")) multiplexer_1 (
    .in0(B), .in1(not_1_out), .out(multiplexer_1_out), .sel(ALUControl[2]));
  assign not_1_out = ~B;  // NOT_Gate not_1, 32 bits wide
  assign and_1_out = multiplexer_1_out & A;  // AND_Gate and_1, 32 bits wide
  assign or_1_out = A | multiplexer_1_out;  // OR_Gate or_1, 32 bits wide
  Adder #(.width(32)) adder_1 (.a(multiplexer_1_out), .b(A), .out(adder_1_out));  // open: cin, cout
  BitSelector #(.width(32)) bitselector_1 (.in(adder_1_out), .out(bitselector_1_out), .sel({5{1'b1}}));
  zeroExtend zeroextend_1 (.A(bitselector_1_out), .Y(zeroextend_1_y));
  Multiplexer #(.select(2), .width(32), .enable("false")) multiplexer_2 (
    .in0(and_1_out), .in1(or_1_out), .in2(adder_1_out), .in3(zeroextend_1_y), .out(Result),
    .sel(ALUControl[1:0]));
  BitSelector #(.width(32)) bitselector_2 (.in(Result), .out(Negative), .sel({5{1'b1}}));
  Or32 or32_1 (.A(Result), .Y(or32_1_y));
  not not_2 (Zero, or32_1_y);
endmodule

module Or32 (
  input  [31:0] A,
  output Y
);

  or or_1 (Y, A[0], A[1], A[2], A[3], A[4], A[5], A[6], A[7], A[8], A[9], A[10], A[11], A[12], A[13], A[14], A[15], A[16], A[17], A[18], A[19], A[20], A[21], A[22], A[23], A[24], A[25], A[26], A[27], A[28], A[29], A[30], A[31]);
endmodule

module zeroExtend (
  input  A,
  output [31:0] Y
);

  assign Y = {{31{1'b0}}, A};  // Bit_Extender bit_extender_1
endmodule

module ALU2 (
  input  [5:0] ALUControl,
  input  [15:0] X,
  input  [15:0] Y,
  output [15:0] OUT1,
  output zr,
  output [15:0] out_6,
  output ng,
  output [15:0] out_8,
  output [15:0] out_9
);

  wire not_1_out;
  wire [15:0] adder_1_out, and_1_out, not_2_out, zxhelper_1_y, zxhelper_2_y;

  zxhelper zxhelper_1 (.Y(zxhelper_1_y), .zx(ALUControl[5]), .in1(X));
  nxHelper nxhelper_1 (.Y(out_8), .nx(ALUControl[4]), .in1(zxhelper_1_y));
  zxhelper zxhelper_2 (.Y(zxhelper_2_y), .zx(ALUControl[3]), .in1(Y));
  nxHelper nxhelper_2 (.Y(out_6), .nx(ALUControl[2]), .in1(zxhelper_2_y));
  Adder #(.width(16)) adder_1 (.a(out_8), .b(out_6), .out(adder_1_out));  // open: cin, cout
  assign and_1_out = out_8 & out_6;  // AND_Gate and_1, 16 bits wide
  not not_1 (not_1_out, ALUControl[1]);
  Multiplexer #(.width(16), .enable("false")) multiplexer_1 (
    .in0(adder_1_out), .in1(and_1_out), .out(out_9), .sel(not_1_out));
  Multiplexer #(.width(16), .enable("false")) multiplexer_2 (
    .in0(out_9), .in1(not_2_out), .out(OUT1), .sel(ALUControl[0]));
  assign not_2_out = ~out_9;  // NOT_Gate not_2, 16 bits wide
  BitSelector #(.width(16)) bitselector_1 (.in(OUT1), .out(ng), .sel(4'b1111));
  or16 or16_1 (.in1(OUT1), .Y(zr));

  // Notes on the sheet:
  //   zx
  //   zy
  //   nx
  //   no
  //   ny
  //   f
  //   x
  //   y
endmodule

module zxhelper (
  input  [15:0] in1,
  input  zx,
  output [15:0] Y
);

  Multiplexer #(.width(16), .enable("false")) multiplexer_1 (.in0(in1), .in1({16{1'b0}}), .out(Y), .sel(zx));
endmodule

module nxHelper (
  input  [15:0] in1,
  input  nx,
  output [15:0] Y
);

  wire [15:0] not_1_out;

  assign not_1_out = ~in1;  // NOT_Gate not_1, 16 bits wide
  Multiplexer #(.width(16), .enable("false")) multiplexer_1 (.in0(in1), .in1(not_1_out), .out(Y), .sel(nx));
endmodule

module or16 (
  input  [15:0] in1,
  output Y
);

  wire or_1_out;

  or or_1 (or_1_out, in1[0], in1[1], in1[2], in1[3], in1[4], in1[5], in1[6], in1[7], in1[8], in1[9], in1[10], in1[11], in1[12], in1[13], in1[14], in1[15]);
  not not_1 (Y, or_1_out);
endmodule
