// Logisim project lesson3.circ as structural Verilog
module srLatch (
  input  R,
  input  S,
  output Q,
  output notQ
);

  nor nor_1 (Q, R, notQ);
  nor nor_2 (notQ, Q, S);
endmodule

module DLatch (
  input  CLK,
  input  D,
  output Q,
  output notQ
);

  wire and_1_out, and_2_out, not_1_out;

  not not_1 (not_1_out, D);
  and and_1 (and_1_out, CLK, not_1_out);
  and and_2 (and_2_out, CLK, D);
  srLatch srlatch_1 (.R(and_1_out), .S(and_2_out), .Q(Q), .notQ(notQ));
endmodule

module DFlipFlop (
  input  CLK,
  input  D,
  output Q
);

  wire dlatch_1_q, not_1_out;

  not not_1 (not_1_out, CLK);
  DLatch dlatch_1 (.CLK(not_1_out), .D(D), .Q(dlatch_1_q));  // open: notQ
  DLatch dlatch_2 (.CLK(CLK), .D(dlatch_1_q), .Q(Q));  // open: notQ
endmodule

module EnabledFlipFlop (
  input  EN,
  input  CLK,
  input  D,
  output Q
);

  wire multiplexer_1_out;

  Multiplexer #(.enable("false")) multiplexer_1 (.in0(Q), .in1(D), .out(multiplexer_1_out), .sel(EN));
  DFlipFlop dflipflop_1 (.CLK(CLK), .D(multiplexer_1_out), .Q(Q));
endmodule

module ResettableFlipFlop (
  input  CLK,
  input  D,
  input  Reset,
  output Q
);

  wire and_1_out, not_1_out;

  not not_1 (not_1_out, Reset);
  and and_1 (and_1_out, D, not_1_out);
  DFlipFlop dflipflop_1 (.CLK(CLK), .D(and_1_out), .Q(Q));
endmodule

module DLatchAsync (
  input  Reset,
  input  CLK,
  input  D,
  output Q,
  output notQ
);

  wire and_1_out, and_2_out, nor_1_out, not_1_out, not_2_out, srlatch_1_q;

  not not_1 (not_1_out, D);
  and and_1 (and_1_out, CLK, not_1_out);
  and and_2 (and_2_out, CLK, D);
  not not_2 (not_2_out, Reset);
  nor nor_1 (nor_1_out, not_2_out, and_1_out);
  srLatch srlatch_1 (.R(nor_1_out), .S(and_2_out), .Q(srlatch_1_q), .notQ(notQ));
  and and_3 (Q, not_2_out, srlatch_1_q);
endmodule

module ResettableDFlipFlopAsync (
  input  CLK,
  input  D,
  input  Reset,
  output Q
);

  wire and_1_out, dlatch_1_q, not_1_out, not_2_out, or_1_out;

  not not_1 (not_1_out, CLK);
  DLatch dlatch_1 (.CLK(not_1_out), .D(D), .Q(dlatch_1_q));  // open: notQ
  and and_1 (and_1_out, dlatch_1_q, not_2_out);
  not not_2 (not_2_out, Reset);
  or or_1 (or_1_out, CLK, Reset);
  DLatch dlatch_2 (.CLK(or_1_out), .D(and_1_out), .Q(Q));  // open: notQ
endmodule

module SettableDFlipFlopSync (
  input  CLK,
  input  D,
  input  S,
  output out_4
);

  wire dlatch_1_q, not_1_out, or_1_out, or_2_out;

  not not_1 (not_1_out, CLK);
  DLatch dlatch_1 (.CLK(not_1_out), .D(D), .Q(dlatch_1_q));  // open: notQ
  or or_1 (or_1_out, dlatch_1_q, S);
  or or_2 (or_2_out, CLK, S);
  DLatch dlatch_2 (.CLK(or_2_out), .D(or_1_out), .Q(out_4));  // open: notQ

  // Other names for the same wires on the sheet: Set = S
endmodule

module DLatchAsyncSet (
  input  CLK,
  input  Set,
  input  D,
  output Q,
  output notQ
);

  wire and_1_out, and_2_out, and_3_out, not_1_out, not_2_out, or_1_out;

  not not_1 (not_1_out, D);
  and and_1 (and_1_out, CLK, not_1_out);
  and and_2 (and_2_out, CLK, D);
  not not_2 (not_2_out, Set);
  and and_3 (and_3_out, and_1_out, not_2_out);
  or or_1 (or_1_out, Set, and_2_out);
  srLatch srlatch_1 (.R(and_3_out), .S(or_1_out), .Q(Q), .notQ(notQ));
endmodule

module AsyncSetDFlipFlop (
  input  CLK,
  input  S,
  input  D,
  output out_4
);

  wire dlatchasyncset_1_q, not_1_out;

  not not_1 (not_1_out, CLK);
  DLatchAsyncSet dlatchasyncset_1 (.CLK(not_1_out), .Set(S), .D(D), .Q(dlatchasyncset_1_q));  // open: notQ
  DLatchAsyncSet dlatchasyncset_2 (.CLK(CLK), .Set(S), .D(dlatchasyncset_1_q), .Q(out_4));  // open: notQ
endmodule

module LogiDTrigger (
  input  Reset,
  input  CLK,
  input  Enable,
  input  Set,
  input  D,
  output Q
);

  wire and_1_out, and_2_out, and_3_out, dlatchasyncset_1_q, not_1_out, not_2_out, or_1_out;

  and and_1 (and_1_out, Set, not_1_out);
  not not_1 (not_1_out, and_3_out);
  not not_2 (not_2_out, Reset);
  DLatchAsyncSet dlatchasyncset_1 (.CLK(not_1_out), .Set(and_1_out), .D(D), .Q(dlatchasyncset_1_q));  // open: notQ
  or or_1 (or_1_out, Reset, and_3_out);
  and and_2 (and_2_out, not_2_out, dlatchasyncset_1_q);
  and and_3 (and_3_out, CLK, Enable);
  DLatchAsyncSet dlatchasyncset_2 (.CLK(or_1_out), .Set(and_1_out), .D(and_2_out), .Q(Q));  // open: notQ
endmodule

module FourBitRegister (
  input  CLK,
  input  [3:0] X,
  output [3:0] Y
);

  DLatch dlatch_1 (.CLK(CLK), .D(X[0]), .Q(Y[0]));  // open: notQ
  DLatch dlatch_2 (.CLK(CLK), .D(X[1]), .Q(Y[1]));  // open: notQ
  DLatch dlatch_3 (.CLK(CLK), .D(X[2]), .Q(Y[2]));  // open: notQ
  DLatch dlatch_4 (.CLK(CLK), .D(X[3]), .Q(Y[3]));  // open: notQ
endmodule

module registerScheme (
  input  [7:0] A,
  input  C,
  input  [7:0] B,
  input  CLK
);

  wire [7:0] adder_1_out, register_1_q, register_2_q, xor_1_out;

  assign xor_1_out = A ^ B;  // XOR_Gate xor_1, 8 bits wide
  Adder adder_1 (.a(register_2_q), .b(xor_1_out), .out(adder_1_out), .cin(C));  // open: cout
  Register register_1 (.D(adder_1_out), .clk(CLK), .Q(register_1_q));  // open: en, clr
  Register register_2 (.D(register_1_q), .clk(CLK), .Q(register_2_q));  // open: en, clr
endmodule

module SyncSeqScheme (
  input  [7:0] I,
  output [7:0] O
);

  wire Button1, CLK_out;
  wire [7:0] adder_1_out, multiplexer_1_out, not_1_out;

  Multiplexer #(.width(8), .enable("false")) multiplexer_1 (
    .in0(I), .in1(not_1_out), .out(multiplexer_1_out), .sel(Button1));
  assign not_1_out = ~I;  // NOT_Gate not_1, 8 bits wide
  Button u_Button1 (.out(Button1));
  Adder adder_1 (.a(O), .b(multiplexer_1_out), .out(adder_1_out), .cin(Button1));  // open: cout
  Register register_1 (.D(adder_1_out), .clk(CLK_out), .Q(O));  // open: en, clr
  Clock CLK (.out(CLK_out));
endmodule

module RAM8 (
  input  load,
  input  [31:0] input1,
  input  [2:0] address,
  output [31:0] output1
);

  wire l0, l1, l2, l3, l4, l5, l6, l7;
  wire [31:0] demultiplexer_2_out0, demultiplexer_2_out1, demultiplexer_2_out2, demultiplexer_2_out3,
       demultiplexer_2_out4, demultiplexer_2_out5, demultiplexer_2_out6, demultiplexer_2_out7, register_1_q,
       register_2_q, register_3_q, register_4_q, register_5_q, register_6_q, register_7_q, register_8_q;

  Demultiplexer #(.select(3), .enable("false")) demultiplexer_1 (
    .out0(l0), .out1(l1), .out2(l2), .out3(l3), .out4(l4), .out5(l5), .out6(l6), .out7(l7), .in(load),
    .sel(address));
  Demultiplexer #(.select(3), .width(32), .enable("false")) demultiplexer_2 (
    .out0(demultiplexer_2_out0), .out1(demultiplexer_2_out1), .out2(demultiplexer_2_out2),
    .out3(demultiplexer_2_out3), .out4(demultiplexer_2_out4), .out5(demultiplexer_2_out5),
    .out6(demultiplexer_2_out6), .out7(demultiplexer_2_out7), .in(input1), .sel(address));
  Register #(.width(32)) register_1 (.D(demultiplexer_2_out0), .clk(l0), .Q(register_1_q));  // open: en, clr
  Register #(.width(32)) register_2 (.D(demultiplexer_2_out2), .clk(l2), .Q(register_2_q));  // open: en, clr
  Register #(.width(32)) register_3 (.D(demultiplexer_2_out4), .clk(l4), .Q(register_3_q));  // open: en, clr
  Register #(.width(32)) register_4 (.D(demultiplexer_2_out6), .clk(l6), .Q(register_4_q));  // open: en, clr
  Register #(.width(32)) register_5 (.D(demultiplexer_2_out1), .clk(l1), .Q(register_5_q));  // open: en, clr
  Register #(.width(32)) register_6 (.D(demultiplexer_2_out3), .clk(l3), .Q(register_6_q));  // open: en, clr
  Register #(.width(32)) register_7 (.D(demultiplexer_2_out5), .clk(l5), .Q(register_7_q));  // open: en, clr
  Register #(.width(32)) register_8 (.D(demultiplexer_2_out7), .clk(l7), .Q(register_8_q));  // open: en, clr
  Multiplexer #(.select(3), .width(32), .enable("false")) multiplexer_1 (
    .in0(register_1_q), .in1(register_5_q), .in2(register_2_q), .in3(register_6_q), .in4(register_3_q),
    .in5(register_7_q), .in6(register_4_q), .in7(register_8_q), .out(output1), .sel(address));
endmodule

module RAM64 (
  input  load,
  input  [31:0] input1,
  input  [5:0] address,
  output [31:0] out1
);

  wire l0, l1, l2, l3, l4, l5, l6, l7;
  wire [31:0] demultiplexer_2_out0, demultiplexer_2_out1, demultiplexer_2_out2, demultiplexer_2_out3,
       demultiplexer_2_out4, demultiplexer_2_out5, demultiplexer_2_out6, demultiplexer_2_out7,
       ram8_1_output1, ram8_2_output1, ram8_3_output1, ram8_4_output1, ram8_5_output1, ram8_6_output1,
       ram8_7_output1, ram8_8_output1;

  Demultiplexer #(.select(3), .enable("false")) demultiplexer_1 (
    .out0(l0), .out1(l1), .out2(l2), .out3(l3), .out4(l4), .out5(l5), .out6(l6), .out7(l7), .in(load),
    .sel(address[5:3]));
  Demultiplexer #(.select(3), .width(32), .enable("false")) demultiplexer_2 (
    .out0(demultiplexer_2_out0), .out1(demultiplexer_2_out1), .out2(demultiplexer_2_out2),
    .out3(demultiplexer_2_out3), .out4(demultiplexer_2_out4), .out5(demultiplexer_2_out5),
    .out6(demultiplexer_2_out6), .out7(demultiplexer_2_out7), .in(input1), .sel(address[5:3]));
  RAM8 ram8_1 (.output1(ram8_1_output1), .address(address[2:0]), .input1(demultiplexer_2_out0), .load(l0));
  RAM8 ram8_2 (.output1(ram8_2_output1), .address(address[2:0]), .input1(demultiplexer_2_out2), .load(l2));
  RAM8 ram8_3 (.output1(ram8_3_output1), .address(address[2:0]), .input1(demultiplexer_2_out4), .load(l4));
  RAM8 ram8_4 (.output1(ram8_4_output1), .address(address[2:0]), .input1(demultiplexer_2_out6), .load(l6));
  RAM8 ram8_5 (.output1(ram8_5_output1), .address(address[2:0]), .input1(demultiplexer_2_out1), .load(l1));
  RAM8 ram8_6 (.output1(ram8_6_output1), .address(address[2:0]), .input1(demultiplexer_2_out3), .load(l3));
  RAM8 ram8_7 (.output1(ram8_7_output1), .address(address[2:0]), .input1(demultiplexer_2_out5), .load(l5));
  RAM8 ram8_8 (.output1(ram8_8_output1), .address(address[2:0]), .input1(demultiplexer_2_out7), .load(l7));
  Multiplexer #(.select(3), .width(32), .enable("false")) multiplexer_1 (
    .in0(ram8_1_output1), .in1(ram8_5_output1), .in2(ram8_2_output1), .in3(ram8_6_output1),
    .in4(ram8_3_output1), .in5(ram8_7_output1), .in6(ram8_4_output1), .in7(ram8_8_output1), .out(out1),
    .sel(address[5:3]));

  // Other names for the same wires on the sheet: address_t[2:0] = address[2:0]; address1[2:0] = address[5:3]

  // Notes on the sheet:
  //   В какой регистр
  //   В каком модуле памяти RAM8
endmodule

module PCBlock (
  input  inc,
  input  load,
  input  reset,
  input  [15:0] input1,
  output [15:0] output1
);

  wire clock_1_out;
  wire [15:0] adder_1_out, multiplexer_1_out, multiplexer_2_out, multiplexer_3_out;

  Adder #(.width(16)) adder_1 (.a(16'h1), .b(output1), .out(adder_1_out));  // open: cin, cout
  Multiplexer #(.width(16), .enable("false")) multiplexer_1 (
    .in0(output1), .in1(adder_1_out), .out(multiplexer_1_out), .sel(inc));
  Multiplexer #(.width(16), .enable("false")) multiplexer_2 (
    .in0(multiplexer_1_out), .in1(input1), .out(multiplexer_2_out), .sel(load));
  Multiplexer #(.width(16), .enable("false")) multiplexer_3 (
    .in0(multiplexer_2_out), .in1({16{1'b0}}), .out(multiplexer_3_out), .sel(reset));
  Register #(.width(16)) register_1 (.D(multiplexer_3_out), .clk(clock_1_out), .Q(output1));  // open: en, clr
  Clock clock_1 (.out(clock_1_out));

  // Notes on the sheet:
  //   Управляющие биты в порядке приоритета
endmodule
