// Logisim project lesson5.circ as structural Verilog: 13 circuits, main circuit main
module main (
  input  [31:0] A,
  input  [31:0] B,
  input  [3:0] op,
  input  [4:0] sa,
  output [31:0] Y
);

  // Mips_ALU mips_alu_1: pin names not known; wires that end beside it: A, B, op, sa, Y
endmodule

module PC (
  input  CLK,
  input  Reset,
  output [31:0] Q
);

  wire [31:0] adder_1_out;

  Register #(.width(32)) register_1 (.D(adder_1_out), .clk(CLK), .Q(Q), .clr(Reset));  // open: en
  Adder #(.width(32)) adder_1 (.a(Q), .b(32'h4), .out(adder_1_out));  // open: cin, cout
endmodule

module PCTest (
  input  Reset,
  output [31:0] Command
);

  wire CLK_out;
  wire [31:0] pc_1_q;

  Clock CLK (.out(CLK_out));
  PC pc_1 (.CLK(CLK_out), .Reset(Reset), .Q(pc_1_q));
  // MIPSProgramROM mipsprogramrom_1: pin names not known; wires that end beside it: pc_1_q, Command

  // Notes on the sheet:
  //   contents of mipsprogramrom_1 (hex, n*v repeats v):
  //   ADDIU $2, $0, 0x38 ADDIU $3, $0, 0x8 ADDIU $4, $0, 0x2 ADDIU $5, $0, 0x1  SLTI $6, $2, 0xf SLTI $7,
  //   $3, 0x8 SLTI $8, $1, 0x80 SLTI $9, $2, 0x800
endmodule

module Decode (
  input  [31:0] instruction,
  output [4:0] rs,
  output [4:0] rt,
  output [4:0] rd,
  output [4:0] shamt,
  output [15:0] imm,
  output [25:0] addr,
  output [5:0] opcode,
  output [5:0] funct
);

  wire comparator_1_eq, not_1_out;
  wire [4:0] rsI, rsR, rtI, rtR;

  Comparator #(.width(6)) comparator_1 (.a({6{1'b0}}), .b(instruction[31:26]), .eq(comparator_1_eq));  // open: gt, lt
  not not_1 (not_1_out, comparator_1_eq);
  RTypeDH rtypedh_1 (.inst(instruction), .funct(funct), .shamt(shamt), .rd(rd), .rt(rtR), .rs(rsR));
  ITypeDH itypedh_1 (.inst(instruction), .imm(imm), .rt(rtI), .rs(rsI));
  JTypeDH jtypedh_1 (.inst(instruction), .addr(addr));
  Multiplexer #(.width(5), .enable("false")) multiplexer_1 (.in0(rsR), .in1(rsI), .out(rs), .sel(not_1_out));
  Multiplexer #(.width(5), .enable("false")) multiplexer_2 (.in0(rtR), .in1(rtI), .out(rt), .sel(not_1_out));

  assign opcode = instruction[31:26];
endmodule

module RTypeDH (
  input  [31:0] inst,
  output [5:0] funct,
  output [4:0] shamt,
  output [4:0] rd,
  output [4:0] rt,
  output [4:0] rs
);


  assign funct = inst[5:0];
  assign rd = inst[15:11];
  assign rs = inst[25:21];
  assign rt = inst[20:16];
  assign shamt = inst[10:6];
endmodule

module ITypeDH (
  input  [31:0] inst,
  output [15:0] imm,
  output [4:0] rt,
  output [4:0] rs
);


  assign imm = inst[15:0];
  assign rs = inst[25:21];
  assign rt = inst[20:16];
endmodule

module JTypeDH (
  input  [31:0] inst,
  output [25:0] addr
);


  assign addr = inst[25:0];
endmodule

module control (
  input  [5:0] opcode,
  output [3:0] ALUOp,
  output RegWrite,
  output ExOp,
  output Slt_U,
  output SLTOp
);

  o_alu o_alu_1 (
    .x5(opcode[5]), .x4(opcode[4]), .x3(opcode[3]), .x2(opcode[2]), .x1(opcode[1]), .x0(opcode[0]),
    .a3(ALUOp[3]), .a2(ALUOp[2]), .a1(ALUOp[1]), .a0(ALUOp[0]));
  o_oth o_oth_1 (
    .x5(opcode[5]), .x4(opcode[4]), .x3(opcode[3]), .x2(opcode[2]), .x1(opcode[1]), .x0(opcode[0]),
    .RegWrite(RegWrite), .ExOp(ExOp), .Slt_U(Slt_U), .SLTOp(SLTOp));
endmodule

module o_alu (
  input  x5,
  input  x4,
  input  x3,
  input  x2,
  input  x1,
  input  x0,
  output a3,
  output a2,
  output a1,
  output a0
);

  wire and_1_out, and_2_out, not_1_out, not_2_out, not_3_out, not_4_out, not_5_out, not_6_out, not_7_out,
       not_8_out, not_9_out, not_10_out, not_11_out;

  not not_1 (not_1_out, x5);
  not not_2 (not_2_out, x4);
  not not_3 (not_3_out, x1);
  not not_4 (not_4_out, x5);
  not not_5 (not_5_out, x4);
  not not_6 (not_6_out, x0);
  not not_7 (not_7_out, x5);
  not not_8 (not_8_out, x4);
  not not_9 (not_9_out, x0);
  not not_10 (not_10_out, x3);
  not not_11 (not_11_out, x2);
  and and_1 (and_1_out, not_1_out, not_2_out, x3, x2, not_3_out);
  and and_2 (and_2_out, not_4_out, not_5_out, x3, x2, not_6_out);
  and and_3 (a2, not_7_out, not_8_out, x3, x2, x1, not_9_out);
  or or_1 (a1, not_10_out, not_11_out, x0, x4, x5);
  or or_2 (a3, and_1_out, and_2_out);

  assign a0 = 1'b0;
endmodule

module o_oth (
  input  x5,
  input  x4,
  input  x3,
  input  x2,
  input  x1,
  input  x0,
  output RegWrite,
  output ExOp,
  output Slt_U,
  output SLTOp
);

  wire not_2_out, not_3_out, not_4_out, not_5_out, not_6_out, not_7_out;

  not not_1 (ExOp, x2);
  not not_2 (not_2_out, x5);
  not not_3 (not_3_out, x4);
  not not_4 (not_4_out, x2);
  not not_5 (not_5_out, x5);
  not not_6 (not_6_out, x4);
  not not_7 (not_7_out, x2);
  and and_1 (Slt_U, not_2_out, not_3_out, x3, not_4_out, x1, x0);
  and and_2 (SLTOp, not_5_out, not_6_out, x3, not_7_out, x1);

  assign RegWrite = 1'b1;
endmodule

module DataPath (
  input  in_1
);

  wire CLK, control_1_exop, control_1_sltop, rw, SLT_u;
  wire [3:0] ALUOp;
  wire [4:0] rs, rt;
  wire [5:0] opcode;
  wire [15:0] imm;
  wire [31:0] bit_extend_1_y, mips_alu_1_p4, pc_1_q, registerfile_1_p1, registerfile_1_p6, slt_1_y;

  Clock clock_1 (.out(CLK));
  PC pc_1 (.CLK(CLK), .Reset(in_1), .Q(pc_1_q));
  // MIPSProgramROM mipsprogramrom_1: pin names not known; wires that end beside it: pc_1_q
  Decode decode_1 (.imm(imm), .rt(rt), .rs(rs), .opcode(opcode));  // open: addr, shamt, rd, instruction, funct
  control control_1 (
    .RegWrite(rw), .ALUOp(ALUOp), .opcode(opcode), .ExOp(control_1_exop), .Slt_U(SLT_u),
    .SLTOp(control_1_sltop));
  // RegisterFile registerfile_1: pin names not known; wires that end beside it: registerfile_1_p1, CLK, rw, rt, rs, registerfile_1_p6
  bit_extend bit_extend_1 (.imm(imm), .ExOp(control_1_exop), .y(bit_extend_1_y));
  // Mips_ALU mips_alu_1: pin names not known; wires that end beside it: registerfile_1_p6, bit_extend_1_y, ALUOp, mips_alu_1_p4
  SLT slt_1 (.A(registerfile_1_p6), .B(bit_extend_1_y), .u(SLT_u), .y(slt_1_y));
  Multiplexer #(.width(32), .enable("false")) multiplexer_1 (
    .in0(mips_alu_1_p4), .in1(slt_1_y), .out(registerfile_1_p1), .sel(control_1_sltop));

  // Notes on the sheet:
  //   contents of mipsprogramrom_1 (hex, n*v repeats v):
  //   ADDIU $2, $zero, -10912 ADDIU $3, $zero, -16837 ADDIU $4, $zero, 24393  SLTIU $5, $1, -20799 SLTIU
  //   $6, $2, -10912 SLTIU $7, $3, -16837 SLTI $8, $4, 24393  SLTIU $5, $2, 10230 SLTI $6, $3, -8073 SLTIU
  //   $7, $2, 25708 SLTIU $8, $2, 9393 SLTIU $9, $1, 9388 SLTIU $10, $3, 9030 SLTI $11, $1, -13847 SLTIU
  //   $12, $3, 24515 SLTI $13, $3, 12504 SLTIU $14, $2, 6849 SLTIU $15, $3, -9869 SLTI $16, $2, -21317
  //   SLTI $17, $3, -13736 SLTIU $18, $2, 2119 SLTIU $19, $3, -26589 SLTI $20, $2, -27763 SLTIU $21, $1,
  //   -14958 SLTIU $22, $2, 3806 SLTI $23, $1, -29446 SLTIU $24, $3, -23798 SLTI $25, $3, 29416 SLTI $26,
  //   $2, 8412 SLTIU $27, $2, -14859 SLTI $28, $1, 21251 SLTI $29, $2, -635 SLTI $30, $2, 28461
endmodule

module bit_extend (
  input  [15:0] imm,
  input  ExOp,
  output [31:0] y
);

  wire [31:0] bit_extender_1_out, bit_extender_2_out;

  assign bit_extender_1_out = {{16{1'b0}}, imm};  // Bit_Extender bit_extender_1
  assign bit_extender_2_out = {{16{imm[15]}}, imm};  // Bit_Extender bit_extender_2
  Multiplexer #(.width(32), .enable("false")) multiplexer_1 (
    .in0(bit_extender_1_out), .in1(bit_extender_2_out), .out(y), .sel(ExOp));
endmodule

module SLT (
  input  [31:0] A,
  input  [31:0] B,
  input  u,
  output [31:0] y
);

  wire comparator_1_eq, comparator_1_gt, comparator_2_eq, comparator_2_gt, multiplexer_1_out, or_1_out,
       or_2_out;

  Comparator #(.width(32)) comparator_1 (.a(A), .b(B), .gt(comparator_1_gt), .eq(comparator_1_eq));  // open: lt
  Comparator #(.width(32), .mode("unsigned")) comparator_2 (
    .a(A), .b(B), .gt(comparator_2_gt), .eq(comparator_2_eq));  // open: lt
  or or_1 (or_1_out, comparator_1_gt, comparator_1_eq);
  or or_2 (or_2_out, comparator_2_gt, comparator_2_eq);
  Multiplexer #(.enable("false")) multiplexer_1 (.in0(or_1_out), .in1(or_2_out), .out(multiplexer_1_out), .sel(u));
  assign y = {{31{1'b0}}, multiplexer_1_out};  // Bit_Extender bit_extender_1
endmodule
