// Logisim project lesson6.circ as structural Verilog: 20 circuits, main circuit main
module main (
  input  [31:0] A,
  input  [31:0] B,
  input  [3:0] op,
  input  [4:0] sa,
  output [31:0] Y
);

  // Mips_ALU mips_alu_1: pin names not known; wires that end beside it: A, B, op, sa, Y
endmodule

module PC (
  input  jmp,
  input  [31:0] addr,
  input  CLK,
  input  Reset,
  output [31:0] Q
);

  wire [31:0] adder_1_out, multiplexer_1_out;

  Adder #(.width(32)) adder_1 (.a(Q), .b(32'h4), .out(adder_1_out));  // open: cin, cout
  Register #(.width(32)) register_1 (.D(multiplexer_1_out), .clk(CLK), .Q(Q), .clr(Reset));  // open: en
  Multiplexer #(.width(32), .enable("false")) multiplexer_1 (
    .in0(adder_1_out), .in1({Q[31:28], addr[27:0]}), .out(multiplexer_1_out), .sel(jmp));

  // Other names for the same wires on the sheet: pcPlus4[31:0] = Q
endmodule

module PCTest (
  input  Reset,
  output [31:0] Command
);

  wire CLK_out, pc_1_p3;

  Clock CLK (.out(CLK_out));
  // PC pc_1: pin names not known; wires that end beside it: CLK_out, Reset, pc_1_p3
  // MIPSProgramROM mipsprogramrom_1: pin names not known; wires that end beside it: pc_1_p3, Command

  // Notes on the sheet:
  //   contents of mipsprogramrom_1 (hex, n*v repeats v):
  //   ADDIU $2, $0, 0x38 ADDIU $3, $0, 0x8 ADDIU $4, $0, 0x2 ADDIU $5, $0, 0x1  SLTI $6, $2, 0xf SLTI $7,
  //   $3, 0x8 SLTI $8, $1, 0x80 SLTI $9, $2, 0x800
endmodule

module Decode (
  input  [31:0] instruction,
  output [4:0] rs,
  output [4:0] rt,
  output [4:0] rd,
  output [4:0] shamt,
  output [15:0] imm,
  output [25:0] addr,
  output [5:0] opcode,
  output [5:0] funct
);

  wire comparator_1_eq, not_1_out;
  wire [4:0] rsI, rsR, rtI, rtR;

  Comparator #(.width(6)) comparator_1 (.a({6{1'b0}}), .b(instruction[31:26]), .eq(comparator_1_eq));  // open: gt, lt
  not not_1 (not_1_out, comparator_1_eq);
  RTypeDH rtypedh_1 (.inst(instruction), .funct(funct), .shamt(shamt), .rd(rd), .rt(rtR), .rs(rsR));
  ITypeDH itypedh_1 (.inst(instruction), .imm(imm), .rt(rtI), .rs(rsI));
  JTypeDH jtypedh_1 (.inst(instruction), .addr(addr));
  Multiplexer #(.width(5), .enable("false")) multiplexer_1 (.in0(rsR), .in1(rsI), .out(rs), .sel(not_1_out));
  Multiplexer #(.width(5), .enable("false")) multiplexer_2 (.in0(rtR), .in1(rtI), .out(rt), .sel(not_1_out));

  assign opcode = instruction[31:26];
endmodule

module RTypeDH (
  input  [31:0] inst,
  output [5:0] funct,
  output [4:0] shamt,
  output [4:0] rd,
  output [4:0] rt,
  output [4:0] rs
);


  assign funct = inst[5:0];
  assign rd = inst[15:11];
  assign rs = inst[25:21];
  assign rt = inst[20:16];
  assign shamt = inst[10:6];
endmodule

module ITypeDH (
  input  [31:0] inst,
  output [15:0] imm,
  output [4:0] rt,
  output [4:0] rs
);


  assign imm = inst[15:0];
  assign rs = inst[25:21];
  assign rt = inst[20:16];
endmodule

module JTypeDH (
  input  [31:0] inst,
  output [25:0] addr
);


  assign addr = inst[25:0];
endmodule

module control (
  input  [5:0] opcode,
  input  [5:0] funct,
  output [3:0] ALUOp,
  output RegWrite,
  output ExOp,
  output Slt_U,
  output SLTOp,
  output RegDst,
  output ALUSrc,
  output shiftVar,
  output MoveZ,
  output isMove,
  output isLui,
  output isJmp,
  output JR,
  output JAL,
  output BEQ,
  output LW,
  output SW
);

  wire OCZero;
  wire [5:0] multiplexer_1_out;

  isOpcodeZero isopcodezero_1 (.in_1(opcode), .out_2(OCZero));
  Multiplexer #(.width(6), .enable("false")) multiplexer_1 (
    .in0(opcode), .in1(funct), .out(multiplexer_1_out), .sel(OCZero));
  o_alu o_alu_1 (
    .x5(multiplexer_1_out[5]), .x4(multiplexer_1_out[4]), .x3(multiplexer_1_out[3]),
    .x2(multiplexer_1_out[2]), .x1(multiplexer_1_out[1]), .x0(multiplexer_1_out[0]), .isOCZero(OCZero),
    .a3(ALUOp[3]), .a2(ALUOp[2]), .a1(ALUOp[1]), .a0(ALUOp[0]));
  o_beq o_beq_1 (
    .x5(multiplexer_1_out[5]), .x4(multiplexer_1_out[4]), .x3(multiplexer_1_out[3]),
    .x2(multiplexer_1_out[2]), .x1(multiplexer_1_out[1]), .x0(multiplexer_1_out[0]), .in_7(OCZero), .BEQ(BEQ));
  o_lw_sw o_lw_sw_1 (
    .in_1(multiplexer_1_out[5]), .in_2(multiplexer_1_out[4]), .in_3(multiplexer_1_out[3]),
    .in_4(multiplexer_1_out[2]), .in_5(multiplexer_1_out[1]), .in_6(multiplexer_1_out[0]), .in_7(OCZero),
    .LW(LW), .SW(SW));
  o_oth o_oth_1 (
    .x5(multiplexer_1_out[5]), .x4(multiplexer_1_out[4]), .x3(multiplexer_1_out[3]),
    .x2(multiplexer_1_out[2]), .x1(multiplexer_1_out[1]), .x0(multiplexer_1_out[0]), .isOCZero(OCZero),
    .RegWrite(RegWrite), .ExOp(ExOp), .Slt_U(Slt_U), .SLTOp(SLTOp), .RegDst(RegDst), .ALUSrc(ALUSrc),
    .shiftVar(shiftVar));
  o_mov o_mov_1 (
    .x5(multiplexer_1_out[5]), .x4(multiplexer_1_out[4]), .x3(multiplexer_1_out[3]),
    .x2(multiplexer_1_out[2]), .x1(multiplexer_1_out[1]), .x0(multiplexer_1_out[0]), .isOCZero(OCZero),
    .moveZ(MoveZ), .isMove(isMove), .isLui(isLui));
  o_jmp o_jmp_1 (
    .x5(multiplexer_1_out[5]), .x4(multiplexer_1_out[4]), .x3(multiplexer_1_out[3]),
    .x2(multiplexer_1_out[2]), .x1(multiplexer_1_out[1]), .x0(multiplexer_1_out[0]), .isOCZero(OCZero),
    .isJmp(isJmp), .JR(JR), .JAL(JAL));
endmodule

module o_alu (
  input  x5,
  input  x4,
  input  x3,
  input  x2,
  input  x1,
  input  x0,
  input  isOCZero,
  output a3,
  output a2,
  output a1,
  output a0
);

  wire and_1_out, and_2_out, and_3_out, and_4_out, and_5_out, and_6_out, and_7_out, and_8_out, and_9_out,
       and_10_out, and_11_out, and_12_out, and_13_out, and_14_out, and_15_out, and_16_out, and_17_out,
       and_18_out, and_19_out, not_1_out, not_2_out, not_3_out, not_4_out, not_5_out, not_6_out, not_7_out,
       not_8_out, not_9_out, not_10_out, not_11_out, not_12_out, not_13_out, not_14_out, not_15_out,
       not_16_out, not_17_out, not_18_out, not_19_out, not_20_out, not_21_out, not_22_out, not_23_out,
       not_24_out, not_25_out, not_26_out, not_27_out, not_28_out, not_29_out, not_30_out, not_31_out,
       not_32_out, not_33_out, not_34_out, not_35_out, not_36_out, not_37_out, not_38_out, not_39_out,
       not_40_out, not_41_out;

  not not_1 (not_1_out, x4);
  not not_2 (not_2_out, x3);
  not not_3 (not_3_out, isOCZero);
  not not_4 (not_4_out, x5);
  not not_5 (not_5_out, x4);
  not not_6 (not_6_out, x1);
  not not_7 (not_7_out, x5);
  not not_8 (not_8_out, x4);
  not not_9 (not_9_out, x0);
  not not_10 (not_10_out, x4);
  not not_11 (not_11_out, x3);
  not not_12 (not_12_out, x5);
  not not_13 (not_13_out, x4);
  not not_14 (not_14_out, x3);
  not not_15 (not_15_out, x4);
  not not_16 (not_16_out, x3);
  not not_17 (not_17_out, x5);
  not not_18 (not_18_out, x4);
  not not_19 (not_19_out, x0);
  not not_20 (not_20_out, x4);
  not not_21 (not_21_out, x3);
  not not_22 (not_22_out, x5);
  not not_23 (not_23_out, x3);
  not not_24 (not_24_out, x1);
  not not_25 (not_25_out, x0);
  not not_26 (not_26_out, isOCZero);
  not not_27 (not_27_out, isOCZero);
  not not_28 (not_28_out, x5);
  not not_29 (not_29_out, x4);
  not not_30 (not_30_out, x3);
  not not_31 (not_31_out, x5);
  not not_32 (not_32_out, x4);
  not not_33 (not_33_out, x3);
  not not_34 (not_34_out, isOCZero);
  not not_35 (not_35_out, x5);
  not not_36 (not_36_out, x4);
  not not_37 (not_37_out, x3);
  and and_1 (and_1_out, not_1_out, not_2_out, x2, not_3_out);
  and and_2 (and_2_out, not_4_out, not_5_out, x2, not_6_out, x0);
  and and_3 (and_3_out, not_7_out, not_8_out, x3, x2, not_9_out);
  and and_4 (and_4_out, x5, not_10_out, not_11_out, x2);
  and and_5 (and_5_out, not_12_out, not_13_out, not_14_out, x1);
  and and_6 (and_6_out, not_15_out, not_16_out, x1, x0);
  and and_7 (and_7_out, not_17_out, not_18_out, x2, x1, not_19_out);
  and and_8 (and_8_out, not_20_out, not_21_out, x2, x1);
  not not_38 (not_38_out, x2);
  not not_39 (not_39_out, x1);
  and and_9 (and_9_out, not_38_out, not_39_out, x0);
  and and_10 (and_10_out, not_22_out, not_23_out, x2, not_24_out, not_25_out, not_26_out);
  and and_11 (and_11_out, x2, x1, x0, not_27_out);
  and and_12 (and_12_out, x3, not_40_out);
  not not_40 (not_40_out, x2);
  and and_13 (and_13_out, x3, x0);
  and and_14 (and_14_out, x5, not_41_out);
  not not_41 (not_41_out, x2);
  and and_15 (and_15_out, x5, x0);
  and and_16 (and_16_out, x5, x3);
  and and_17 (and_17_out, not_28_out, not_29_out, not_30_out, x1, x0);
  and and_18 (and_18_out, not_31_out, not_32_out, not_33_out, x2, not_34_out);
  and and_19 (and_19_out, not_35_out, not_36_out, not_37_out, x2, x0);
  or or_1 (a3, and_1_out, and_2_out, and_3_out, and_4_out);
  or or_2 (a2, and_5_out, and_6_out, and_7_out, and_8_out);
  or or_3 (a0, and_17_out, and_18_out, and_19_out);
  or or_4 (a1, and_9_out, and_10_out, and_11_out, and_12_out, and_13_out, x4, and_14_out, and_15_out, and_16_out);
endmodule

module o_oth (
  input  x5,
  input  x4,
  input  x3,
  input  x2,
  input  x1,
  input  x0,
  input  isOCZero,
  output RegWrite,
  output ExOp,
  output Slt_U,
  output SLTOp,
  output RegDst,
  output ALUSrc,
  output shiftVar
);

  wire and_1_out, and_4_out, and_5_out, and_6_out, and_7_out, and_8_out, and_9_out, and_10_out, and_11_out,
       and_12_out, and_13_out, not_1_out, not_2_out, not_3_out, not_4_out, not_5_out, not_6_out, not_7_out,
       not_8_out, not_9_out, not_10_out, not_11_out, not_12_out, not_13_out, not_14_out, not_15_out,
       not_16_out, not_17_out, not_18_out, not_19_out, not_20_out, not_21_out, not_22_out, not_23_out,
       not_24_out, not_25_out, not_26_out, not_27_out, not_28_out, not_29_out, not_30_out, not_31_out;

  not not_1 (not_1_out, x5);
  not not_2 (not_2_out, x4);
  not not_3 (not_3_out, x3);
  not not_4 (not_4_out, x1);
  not not_5 (not_5_out, x0);
  not not_6 (not_6_out, x4);
  not not_7 (not_7_out, x2);
  not not_8 (not_8_out, x4);
  not not_9 (not_9_out, x2);
  not not_10 (not_10_out, x5);
  not not_11 (not_11_out, x4);
  not not_12 (not_12_out, x2);
  not not_13 (not_13_out, x0);
  not not_14 (not_14_out, x5);
  not not_15 (not_15_out, x4);
  not not_16 (not_16_out, x3);
  not not_17 (not_17_out, x4);
  not not_18 (not_18_out, x3);
  not not_19 (not_19_out, x0);
  not not_20 (not_20_out, x4);
  not not_21 (not_21_out, x2);
  not not_22 (not_22_out, x4);
  not not_23 (not_23_out, x3);
  not not_24 (not_24_out, x5);
  not not_25 (not_25_out, x1);
  not not_26 (not_26_out, x3);
  not not_27 (not_27_out, x2);
  not not_28 (not_28_out, x0);
  not not_29 (not_29_out, x5);
  not not_30 (not_30_out, x1);
  and and_1 (and_1_out, not_1_out, not_2_out, not_3_out, not_4_out, not_5_out);
  not not_31 (not_31_out, x2);
  and and_2 (Slt_U, not_6_out, x3, not_7_out, x1, x0);
  and and_3 (SLTOp, not_8_out, x3, not_9_out, x1);
  and and_4 (and_4_out, not_10_out, not_11_out, not_12_out, not_13_out);
  and and_5 (and_5_out, not_14_out, not_15_out, not_16_out, x1);
  and and_6 (and_6_out, not_17_out, not_18_out, x2, not_19_out);
  and and_7 (and_7_out, not_20_out, x3, not_21_out, x1);
  and and_8 (and_8_out, x5, not_22_out, not_23_out, x0);
  and and_9 (and_9_out, not_24_out, not_25_out);
  and and_10 (and_10_out, not_26_out, not_27_out, not_28_out);
  and and_11 (and_11_out, not_29_out, x2);
  and and_12 (and_12_out, x3, not_30_out);
  and and_13 (and_13_out, x3, x2);
  or or_1 (ExOp, and_1_out, not_31_out);
  or or_2 (RegDst, and_4_out, and_5_out, and_6_out, and_7_out, and_8_out);
  or or_3 (ALUSrc, and_9_out, and_10_out, and_11_out, and_12_out, and_13_out, x4);

  assign RegWrite = 1'b1;
  assign shiftVar = x2;
endmodule

module DataPath (
  input  reset
);

  wire ALUSrc, and_1_out, and_2_out, and_3_out, and_4_out, BEQ, bitselector_1_out, CLK, ExOp, isJmp, isLui,
       IsMove, isopcodezero_1_out_2, isopcodezero_2_out_2, JAL, JR, LW, MoveZ, multiplexer_3_out, not_1_out,
       not_2_out, not_3_out, not_4_out, not_5_out, or_1_out, RegDst, rw, shiftVar, SLT_u, SLTOp, SW, wasMoved;
  wire [3:0] ALUOp;
  wire [4:0] multiplexer_9_out, rd, registerfile_1_p5, rs, rt, SA, shamt;
  wire [5:0] funct, opcode;
  wire [15:0] imm;
  wire [25:0] addr;
  wire [31:0] A, adrJMP, B, bit_extender_1_out, immPC, immXtend, LUIOut, lwImm, mips_alu_1_p6,
       multiplexer_1_out, multiplexer_4_out, multiplexer_5_out, multiplexer_7_out, multiplexer_8_out,
       multiplexer_11_out, multiplexer_12_out, PCLabel, PCPlus4, RAMOut, result, shifter_1_out,
       shifter_2_out, slt_1_y;

  Clock clock_1 (.out(CLK));
  assign bit_extender_1_out = {{6{1'b0}}, addr};  // Bit_Extender bit_extender_1
  Adder #(.width(32)) adder_1 (.a(PCLabel), .b(32'h4), .out(PCPlus4));  // open: cin, cout
  BitSelector #(.width(32)) bitselector_1 (.in(result), .out(bitselector_1_out), .sel({5{1'b0}}));
  and and_1 (and_1_out, BEQ, bitselector_1_out);
  Multiplexer #(.width(32), .enable("false")) multiplexer_1 (
    .in0(adrJMP), .in1(immPC), .out(multiplexer_1_out), .sel(and_1_out));
  Shifter #(.width(32)) shifter_1 (.in(bit_extender_1_out), .\dist (5'b00010), .out(shifter_1_out));
  Multiplexer #(.width(32), .enable("false")) multiplexer_2 (.in0(shifter_1_out), .in1(A), .out(adrJMP), .sel(JR));
  Shifter #(.width(32)) shifter_2 (.in(immXtend), .\dist (5'b00010), .out(shifter_2_out));
  Adder #(.width(32)) adder_2 (.a(A), .b(immXtend), .out(lwImm));  // open: cin, cout
  Multiplexer #(.enable("false")) multiplexer_3 (.in0(isJmp), .in1(1'b1), .out(multiplexer_3_out), .sel(and_1_out));
  Adder #(.width(32)) adder_3 (.a(shifter_2_out), .b(PCPlus4), .out(immPC));  // open: cin, cout
  PC pc_1 (.jmp(multiplexer_3_out), .addr(multiplexer_1_out), .CLK(CLK), .Reset(reset), .Q(PCLabel));
  // MIPSProgramROM mipsprogramrom_1: pin names not known; wires that end beside it: PCLabel
  Decode decode_1 (
    .addr(addr), .rd(rd), .rt(rt), .imm(imm), .shamt(shamt), .rs(rs), .opcode(opcode), .funct(funct));  // open: instruction
  control control_1 (
    .opcode(opcode), .funct(funct), .ALUOp(ALUOp), .RegWrite(rw), .ExOp(ExOp), .Slt_U(SLT_u), .SLTOp(SLTOp),
    .RegDst(RegDst), .ALUSrc(ALUSrc), .shiftVar(shiftVar), .MoveZ(MoveZ), .isMove(IsMove), .isLui(isLui),
    .isJmp(isJmp), .JR(JR), .JAL(JAL), .BEQ(BEQ), .LW(LW), .SW(SW));
  // MIPS_RAM #(.addrWidth(24)) mips_ram_1: pin names not known; wires that end beside it: lwImm[23:0], B, SW, CLK, LW, reset, RAMOut
  Multiplexer #(.width(32), .enable("false")) multiplexer_4 (
    .in0(result), .in1(A), .out(multiplexer_4_out), .sel(and_2_out));
  and and_2 (and_2_out, wasMoved, IsMove);
  Multiplexer #(.width(32), .enable("false")) multiplexer_5 (
    .in0(multiplexer_4_out), .in1(LUIOut), .out(multiplexer_5_out), .sel(isLui));
  Multiplexer #(.width(5), .enable("false")) multiplexer_6 (.in0(shamt), .in1(A[4:0]), .out(SA), .sel(shiftVar));
  Multiplexer #(.width(32), .enable("false")) multiplexer_7 (
    .in0(multiplexer_5_out), .in1(PCPlus4), .out(multiplexer_7_out), .sel(JAL));
  Multiplexer #(.width(32), .enable("false")) multiplexer_8 (
    .in0(multiplexer_7_out), .in1(RAMOut), .out(multiplexer_8_out), .sel(LW));
  not not_1 (not_1_out, LW);
  bit_extend bit_extend_1 (.imm(imm), .ExOp(ExOp), .y(immXtend));
  and and_3 (and_3_out, not_2_out, not_3_out, rw, or_1_out);
  not not_2 (not_2_out, SW);
  not not_3 (not_3_out, BEQ);
  or or_1 (or_1_out, wasMoved, not_4_out);
  not not_4 (not_4_out, IsMove);
  LUI lui_1 (.imm(imm), .out1(LUIOut));
  // RegisterFile registerfile_1: pin names not known; wires that end beside it: multiplexer_8_out, CLK, IsMove, and_3_out, registerfile_1_p5, rs, rt, A, B
  Multiplexer #(.width(5), .enable("false")) multiplexer_9 (
    .in0(rt), .in1(rd), .out(multiplexer_9_out), .sel(and_4_out));
  Multiplexer #(.width(5), .enable("false")) multiplexer_10 (
    .in0(multiplexer_9_out), .in1({5{1'b1}}), .out(registerfile_1_p5), .sel(JAL));
  mov mov_1 (.inp1(B), .moveZ(MoveZ), .moved(wasMoved));
  and and_4 (and_4_out, isopcodezero_1_out_2, RegDst);
  isOpcodeZero isopcodezero_1 (.in_1(opcode), .out_2(isopcodezero_1_out_2));
  Multiplexer #(.width(32), .enable("false")) multiplexer_11 (
    .in0(B), .in1(immXtend), .out(multiplexer_11_out), .sel(not_5_out));
  Multiplexer #(.width(32), .enable("false")) multiplexer_12 (
    .in0(multiplexer_11_out), .in1(B), .out(multiplexer_12_out), .sel(BEQ));
  not not_5 (not_5_out, isopcodezero_2_out_2);
  isOpcodeZero isopcodezero_2 (.in_1(opcode), .out_2(isopcodezero_2_out_2));
  // Mips_ALU mips_alu_1: pin names not known; wires that end beside it: ALUSrc, A, multiplexer_12_out, ALUOp, SA, mips_alu_1_p6
  SLT slt_1 (.A(A), .B(multiplexer_12_out), .u(SLT_u), .y(slt_1_y));
  Multiplexer #(.width(32), .enable("false")) multiplexer_13 (
    .in0(mips_alu_1_p6), .in1(slt_1_y), .out(result), .sel(SLTOp));

  // Notes on the sheet:
  //   contents of mipsprogramrom_1 (hex, n*v repeats v):
  //   addiu $v0,$a0,2   # test addi, set $v0  addu  $v0,$v0,$a0  # start of counter. Should be 10 loop:
  //   beq  $v0,$a0,done # test, jump to done.          addiu $v0,$v0,-3   # decrement. Loops twice.
  //   beq  $0,$0,loop   # emulating an unconditional jump done: addu  $0,$0,$0    # NOP
  //   фикс конфликтов LW и SLT
  //   если есть
endmodule

module bit_extend (
  input  [15:0] imm,
  input  ExOp,
  output [31:0] y
);

  wire [31:0] bit_extender_1_out, bit_extender_2_out;

  assign bit_extender_1_out = {{16{1'b0}}, imm};  // Bit_Extender bit_extender_1
  assign bit_extender_2_out = {{16{imm[15]}}, imm};  // Bit_Extender bit_extender_2
  Multiplexer #(.width(32), .enable("false")) multiplexer_1 (
    .in0(bit_extender_1_out), .in1(bit_extender_2_out), .out(y), .sel(ExOp));
endmodule

module SLT (
  input  [31:0] A,
  input  [31:0] B,
  input  u,
  output [31:0] y
);

  wire comparator_1_lt, comparator_2_lt, multiplexer_1_out;

  Comparator #(.width(32)) comparator_1 (.a(A), .b(B), .lt(comparator_1_lt));  // open: gt, eq
  Comparator #(.width(32), .mode("unsigned")) comparator_2 (.a(A), .b(B), .lt(comparator_2_lt));  // open: gt, eq
  Multiplexer #(.enable("false")) multiplexer_1 (
    .in0(comparator_1_lt), .in1(comparator_2_lt), .out(multiplexer_1_out), .sel(u));
  assign y = {{31{1'b0}}, multiplexer_1_out};  // Bit_Extender bit_extender_1
endmodule

module isOpcodeZero (
  input  [5:0] in_1,
  output out_2
);

  nor nor_1 (out_2, in_1[0], in_1[1], in_1[2], in_1[3], in_1[4], in_1[5]);
endmodule

module mov (
  input  [31:0] inp1,
  input  moveZ,
  output moved
);

  wire comparator_1_eq, not_1_out;

  Comparator #(.width(32)) comparator_1 (.a(inp1), .b({32{1'b0}}), .eq(comparator_1_eq));  // open: gt, lt
  not not_1 (not_1_out, comparator_1_eq);
  Multiplexer #(.enable("false")) multiplexer_1 (.in0(not_1_out), .in1(comparator_1_eq), .out(moved), .sel(moveZ));
endmodule

module o_mov (
  input  x5,
  input  x4,
  input  x3,
  input  x2,
  input  x1,
  input  x0,
  input  isOCZero,
  output moveZ,
  output isMove,
  output isLui
);

  wire not_1_out, not_2_out, not_3_out, not_4_out, not_5_out, not_6_out, not_7_out, not_8_out, not_9_out,
       not_10_out;

  not not_1 (not_1_out, x5);
  not not_2 (not_2_out, x4);
  not not_3 (not_3_out, x2);
  not not_4 (not_4_out, x0);
  not not_5 (not_5_out, x5);
  not not_6 (not_6_out, x4);
  not not_7 (not_7_out, x2);
  not not_8 (not_8_out, x5);
  not not_9 (not_9_out, x4);
  not not_10 (not_10_out, isOCZero);
  and and_1 (moveZ, not_1_out, not_2_out, x3, not_3_out, x1, not_4_out, isOCZero);
  and and_2 (isMove, not_5_out, not_6_out, x3, not_7_out, x1, isOCZero);
  and and_3 (isLui, not_8_out, not_9_out, x3, x2, x1, x0, not_10_out);
endmodule

module LUI (
  input  [15:0] imm,
  output [31:0] out1
);

  wire [31:0] bit_extender_1_out;

  assign bit_extender_1_out = {{16{1'b0}}, imm};  // Bit_Extender bit_extender_1
  Shifter #(.width(32)) shifter_1 (.in(bit_extender_1_out), .\dist (5'b10000), .out(out1));
endmodule

module o_jmp (
  input  x5,
  input  x4,
  input  x3,
  input  x2,
  input  x1,
  input  x0,
  input  isOCZero,
  output isJmp,
  output JR,
  output JAL
);

  wire and_1_out, and_2_out, and_3_out, and_4_out, not_1_out, not_2_out, not_3_out, not_4_out, not_5_out,
       not_6_out, not_7_out, not_8_out, not_9_out, not_10_out, not_11_out, not_12_out, not_13_out,
       not_14_out, not_15_out, not_16_out, not_17_out, not_18_out, not_19_out, not_20_out;

  not not_1 (not_1_out, x5);
  not not_2 (not_2_out, x4);
  not not_3 (not_3_out, x3);
  not not_4 (not_4_out, x2);
  not not_5 (not_5_out, x0);
  and and_1 (and_1_out, not_1_out, not_2_out, not_3_out, not_4_out, x1, not_5_out, not_6_out);
  not not_6 (not_6_out, isOCZero);
  not not_7 (not_7_out, x5);
  not not_8 (not_8_out, x4);
  not not_9 (not_9_out, x2);
  and and_2 (and_2_out, not_7_out, not_8_out, x3, not_9_out, not_10_out, not_11_out, isOCZero);
  not not_10 (not_10_out, x1);
  not not_11 (not_11_out, x0);
  not not_12 (not_12_out, x5);
  not not_13 (not_13_out, x4);
  not not_14 (not_14_out, x3);
  not not_15 (not_15_out, x2);
  and and_3 (and_3_out, not_12_out, not_13_out, not_14_out, not_15_out, x1, x0, not_16_out);
  not not_16 (not_16_out, isOCZero);
  not not_17 (not_17_out, x5);
  not not_18 (not_18_out, x4);
  not not_19 (not_19_out, x2);
  and and_4 (and_4_out, not_17_out, not_18_out, x3, not_19_out, not_20_out, x0, isOCZero);
  not not_20 (not_20_out, x1);
  or or_1 (isJmp, and_1_out, and_3_out, and_2_out, and_4_out);
  or or_2 (JR, and_2_out, and_4_out);
  or or_3 (JAL, and_3_out, and_4_out);
endmodule

module o_beq (
  input  x5,
  input  x4,
  input  x3,
  input  x2,
  input  x1,
  input  x0,
  input  in_7,
  output BEQ
);

  wire and_1_out, and_2_out, and_3_out, and_4_out, not_1_out, not_2_out, not_3_out, not_4_out, not_5_out,
       not_6_out, not_7_out, not_8_out, not_9_out, not_10_out, not_11_out, not_12_out, not_13_out,
       not_14_out, not_15_out, not_16_out, not_17_out, not_18_out, not_19_out, not_20_out;

  not not_1 (not_1_out, x5);
  not not_2 (not_2_out, x4);
  not not_3 (not_3_out, x3);
  and and_1 (and_1_out, not_1_out, not_2_out, not_3_out, x2, not_4_out, not_5_out, not_6_out);
  not not_4 (not_4_out, x1);
  not not_5 (not_5_out, x0);
  not not_6 (not_6_out, in_7);
  not not_7 (not_7_out, x5);
  not not_8 (not_8_out, x4);
  not not_9 (not_9_out, x3);
  and and_2 (and_2_out, not_7_out, not_8_out, not_9_out, x2, not_10_out, x0, not_11_out);
  not not_10 (not_10_out, x1);
  not not_11 (not_11_out, in_7);
  not not_12 (not_12_out, x5);
  not not_13 (not_13_out, x4);
  not not_14 (not_14_out, x3);
  and and_3 (and_3_out, not_12_out, not_13_out, not_14_out, x2, x1, not_15_out, not_16_out);
  not not_15 (not_15_out, x0);
  not not_16 (not_16_out, in_7);
  not not_17 (not_17_out, x5);
  not not_18 (not_18_out, x4);
  not not_19 (not_19_out, x3);
  not not_20 (not_20_out, in_7);
  or or_1 (BEQ, and_1_out, and_2_out, and_3_out, and_4_out);
  and and_4 (and_4_out, not_17_out, not_18_out, not_19_out, x2, x1, x0, not_20_out);

  // Other names for the same wires on the sheet: isOCZero = in_7
endmodule

module o_lw_sw (
  input  in_1,
  input  in_2,
  input  in_3,
  input  in_4,
  input  in_5,
  input  in_6,
  input  in_7,
  output LW,
  output SW
);

  wire not_1_out, not_2_out, not_3_out, not_4_out, not_5_out, not_6_out, not_7_out;

  not not_1 (not_1_out, in_2);
  not not_2 (not_2_out, in_3);
  not not_3 (not_3_out, in_4);
  and and_1 (LW, in_1, not_1_out, not_2_out, not_3_out, in_5, in_6, not_4_out);
  not not_4 (not_4_out, in_7);
  not not_5 (not_5_out, in_2);
  not not_6 (not_6_out, in_4);
  and and_2 (SW, in_1, not_5_out, in_3, not_6_out, in_5, in_6, not_7_out);
  not not_7 (not_7_out, in_7);

  // Other names for the same wires on the sheet: isOCZero = in_7; x0 = in_6; x1 = in_5; x2 = in_4; x3 = in_3;
  //   x4 = in_2; x5 = in_1
endmodule
