// Logisim project moore.circ as structural Verilog
module mooreBinary (
  input  in1,
  output out_2
);

  wire and_1_out, and_2_out, and_3_out, and_4_out, and_5_out, and_6_out, and_7_out, clock_1_out, not_1_out,
       not_2_out, not_3_out, not_4_out, not_5_out, not_6_out, not_7_out, not_8_out, not_9_out, not_10_out,
       not_11_out, not_12_out, not_13_out, not_14_out, or_1_out, or_2_out, S0_q, S1_q;

  not not_1 (not_1_out, out_2);
  not not_2 (not_2_out, in1);
  not not_3 (not_3_out, S1_q);
  not not_4 (not_4_out, S0_q);
  not not_5 (not_5_out, in1);
  not not_6 (not_6_out, out_2);
  not not_7 (not_7_out, S0_q);
  not not_8 (not_8_out, S0_q);
  not not_9 (not_9_out, S1_q);
  and and_1 (and_1_out, not_8_out, not_9_out, in1);
  not not_10 (not_10_out, S0_q);
  and and_2 (and_2_out, not_10_out, not_11_out, in1);
  not not_11 (not_11_out, out_2);
  not not_12 (not_12_out, S1_q);
  not not_13 (not_13_out, out_2);
  and and_3 (and_3_out, not_12_out, not_13_out, in1);
  and and_4 (and_4_out, not_1_out, S0_q, not_2_out);
  and and_5 (and_5_out, out_2, not_3_out, not_4_out, not_5_out);
  and and_6 (and_6_out, not_6_out, S1_q, not_7_out, in1);
  not not_14 (not_14_out, out_2);
  and and_7 (and_7_out, not_14_out, S1_q, S0_q, in1);
  or or_1 (or_1_out, and_1_out, and_2_out, and_3_out);
  Clock clock_1 (.out(clock_1_out));
  or or_2 (or_2_out, and_4_out, and_5_out, and_6_out);
  D_Flip_Flop S0 (.D(or_1_out), .clk(clock_1_out), .Q(S0_q));  // open: Qn, preset, reset
  D_Flip_Flop S1 (.D(or_2_out), .clk(clock_1_out), .Q(S1_q));  // open: Qn, preset, reset
  D_Flip_Flop S2 (.D(and_7_out), .clk(clock_1_out), .Q(out_2));  // open: Qn, preset, reset
endmodule

module mealyBin (
  input  in1,
  output out1
);

  wire and_1_out, and_2_out, clock_1_out, not_1_out, not_2_out, or_1_out, S0_q, S1_q;

  and and_1 (and_1_out, S0_q, not_1_out);
  not not_1 (not_1_out, in1);
  and and_2 (and_2_out, S1_q, not_2_out);
  not not_2 (not_2_out, S0_q);
  or or_1 (or_1_out, and_1_out, and_2_out);
  Clock clock_1 (.out(clock_1_out));
  D_Flip_Flop S0 (.D(in1), .clk(clock_1_out), .Q(S0_q));  // open: Qn, preset, reset
  D_Flip_Flop S1 (.D(or_1_out), .clk(clock_1_out), .Q(S1_q));  // open: Qn, preset, reset
  and and_3 (out1, S0_q, S1_q, in1);
endmodule

module mealyHOT (
  input  in1,
  output out1
);

  wire and_1_out, and_2_out, and_3_out, and_4_out, and_5_out, and_6_out, and_7_out, and_8_out, clock_1_out,
       not_1_out, not_2_out, not_3_out, not_4_out, or_1_out, or_2_out, or_3_out, S0_q, S1_q, S2_q, S3_q;

  and and_1 (and_1_out, S0_q, not_1_out);
  not not_1 (not_1_out, in1);
  and and_2 (and_2_out, S2_q, not_2_out);
  not not_2 (not_2_out, in1);
  and and_3 (and_3_out, S0_q, in1);
  and and_4 (and_4_out, S1_q, in1);
  and and_5 (and_5_out, S3_q, in1);
  not not_3 (not_3_out, in1);
  not not_4 (not_4_out, in1);
  and and_6 (and_6_out, S1_q, not_3_out);
  or or_1 (or_1_out, and_6_out, and_7_out);
  and and_7 (and_7_out, S2_q, not_4_out);
  and and_8 (and_8_out, S2_q, in1);
  or or_2 (or_2_out, and_1_out, and_2_out);
  or or_3 (or_3_out, and_3_out, and_4_out, and_5_out);
  Clock clock_1 (.out(clock_1_out));
  D_Flip_Flop S0 (.D(or_2_out), .clk(clock_1_out), .Q(S0_q));  // open: Qn, preset, reset
  D_Flip_Flop S1 (.D(or_3_out), .clk(clock_1_out), .Q(S1_q));  // open: Qn, preset, reset
  D_Flip_Flop S2 (.D(or_1_out), .clk(clock_1_out), .Q(S2_q));  // open: Qn, preset, reset
  D_Flip_Flop S3 (.D(and_8_out), .clk(clock_1_out), .Q(S3_q));  // open: Qn, preset, reset
  and and_9 (out1, S3_q, in1);
endmodule

module mooreHOT (
  input  in_1,
  output out_2
);

  wire and_1_out, and_2_out, and_3_out, and_4_out, and_5_out, and_6_out, and_7_out, and_8_out, and_9_out,
       clock_1_out, d_ff_1_q, d_ff_2_q, d_ff_3_q, d_ff_4_q, not_1_out, not_2_out, not_3_out, not_4_out,
       not_5_out, not_6_out, not_7_out, not_8_out, not_9_out, not_10_out, not_11_out, not_12_out, not_13_out,
       not_14_out, not_15_out, not_16_out, not_17_out, not_18_out, not_19_out, not_20_out, not_21_out,
       not_22_out, not_23_out, not_24_out, not_25_out, not_26_out, not_27_out, not_28_out, not_29_out,
       not_30_out, not_31_out, not_32_out, not_33_out, not_34_out, not_35_out, not_36_out, not_37_out,
       not_38_out, not_39_out, not_40_out, not_41_out, or_1_out, or_2_out, or_3_out;

  not not_1 (not_1_out, out_2);
  not not_2 (not_2_out, d_ff_4_q);
  not not_3 (not_3_out, d_ff_3_q);
  not not_4 (not_4_out, d_ff_2_q);
  not not_5 (not_5_out, in_1);
  not not_6 (not_6_out, out_2);
  not not_7 (not_7_out, d_ff_4_q);
  not not_8 (not_8_out, d_ff_2_q);
  not not_9 (not_9_out, d_ff_1_q);
  not not_10 (not_10_out, in_1);
  not not_11 (not_11_out, out_2);
  not not_12 (not_12_out, d_ff_4_q);
  not not_13 (not_13_out, d_ff_3_q);
  not not_14 (not_14_out, d_ff_2_q);
  not not_15 (not_15_out, out_2);
  not not_16 (not_16_out, d_ff_4_q);
  not not_17 (not_17_out, d_ff_3_q);
  not not_18 (not_18_out, d_ff_1_q);
  not not_19 (not_19_out, out_2);
  not not_20 (not_20_out, d_ff_4_q);
  not not_21 (not_21_out, d_ff_3_q);
  not not_22 (not_22_out, d_ff_1_q);
  not not_23 (not_23_out, in_1);
  not not_24 (not_24_out, out_2);
  not not_25 (not_25_out, d_ff_3_q);
  not not_26 (not_26_out, d_ff_2_q);
  not not_27 (not_27_out, d_ff_1_q);
  not not_28 (not_28_out, in_1);
  not not_29 (not_29_out, d_ff_4_q);
  not not_30 (not_30_out, d_ff_3_q);
  not not_31 (not_31_out, d_ff_2_q);
  not not_32 (not_32_out, d_ff_1_q);
  not not_33 (not_33_out, in_1);
  not not_34 (not_34_out, out_2);
  not not_35 (not_35_out, d_ff_4_q);
  not not_36 (not_36_out, d_ff_2_q);
  not not_37 (not_37_out, d_ff_1_q);
  not not_38 (not_38_out, out_2);
  not not_39 (not_39_out, d_ff_3_q);
  not not_40 (not_40_out, d_ff_2_q);
  not not_41 (not_41_out, d_ff_1_q);
  and and_1 (and_1_out, not_1_out, not_2_out, not_3_out, not_4_out, d_ff_1_q, not_5_out);
  and and_2 (and_2_out, not_6_out, not_7_out, d_ff_3_q, not_8_out, not_9_out, not_10_out);
  and and_3 (and_3_out, not_11_out, not_12_out, not_13_out, not_14_out, d_ff_1_q, in_1);
  and and_4 (and_4_out, not_15_out, not_16_out, not_17_out, d_ff_2_q, not_18_out, in_1);
  and and_5 (and_5_out, not_19_out, not_20_out, not_21_out, d_ff_2_q, not_22_out, not_23_out);
  and and_6 (and_6_out, not_24_out, d_ff_4_q, not_25_out, not_26_out, not_27_out, not_28_out);
  and and_7 (and_7_out, out_2, not_29_out, not_30_out, not_31_out, not_32_out, not_33_out);
  and and_8 (and_8_out, not_34_out, not_35_out, d_ff_3_q, not_36_out, not_37_out, in_1);
  and and_9 (and_9_out, not_38_out, d_ff_4_q, not_39_out, not_40_out, not_41_out, in_1);
  or or_1 (or_1_out, and_1_out, and_2_out);
  or or_2 (or_2_out, and_3_out, and_4_out);
  or or_3 (or_3_out, and_5_out, and_6_out, and_7_out);
  Clock clock_1 (.out(clock_1_out));
  D_Flip_Flop d_ff_1 (.D(or_1_out), .clk(clock_1_out), .Q(d_ff_1_q));  // open: Qn, preset, reset
  D_Flip_Flop d_ff_2 (.D(or_2_out), .clk(clock_1_out), .Q(d_ff_2_q));  // open: Qn, preset, reset
  D_Flip_Flop d_ff_3 (.D(or_3_out), .clk(clock_1_out), .Q(d_ff_3_q));  // open: Qn, preset, reset
  D_Flip_Flop d_ff_4 (.D(and_8_out), .clk(clock_1_out), .Q(d_ff_4_q));  // open: Qn, preset, reset
  D_Flip_Flop d_ff_5 (.D(and_9_out), .clk(clock_1_out), .Q(out_2));  // open: Qn, preset, reset
endmodule
